# Fritzing sketch controlpcvolumewithdualultrasensorarduinoandpython (saved by Fritzing 0.9.3b)
breadboards: 1

parts:
  부품1 = Arduino Uno (Rev3)
  hc-sr1 = hc-sr04
  hc-sr2 = hc-sr04

nets:
  N1: 부품1.D8, hc-sr2.Trig
  N2: 부품1.D9_PWM, hc-sr2.Echo
  N3: 부품1.D2, hc-sr1.Trig
  N4: 부품1.D3_PWM, hc-sr1.Echo
  VCC: 부품1.5V, hc-sr1.VCC, hc-sr2.VCC
  GND: 부품1.GND, hc-sr1.GND, hc-sr2.GND
